# Fritzing sketch treadmill version2 (saved by Fritzing 0.9.3b)
breadboards: 1

parts:
  Raspberry_Pi_1 = Raspberry Pi 3 [part_number=RPI-3-V1.2]
  Treadmill_Connector = Header 8 [package=1x08_smd]
  Safety_Switch_Connector = Header 3 [package=screwterminal-3.5mm-3_lock.007s]
  LM1085 = Voltage Regulator - 5V [package="TO220 [THT]"]
  C1 = Tantalum Capacitor [capacitance=10µF package="100 mil [THT, tantalum]"]
  C2 = Electrolytic Capacitor [capacitance=10µF package="100 mil [THT, electrolytic]"]
  X1 = USB Connectors [package=usb-microb]
  R1 = Resistor [tolerance=±5% resistance=1k package=THT]
  R2 = Resistor [tolerance=±5% resistance=1k package=THT]
  R3 = Resistor [tolerance=±5% resistance=1k package=THT]
  R4 = Resistor [tolerance=±5% resistance=100 package=THT]
  C3 = Ceramic Capacitor [capacitance=20nF package="100 mil [THT, multilayer]"]

nets:
  GND: Raspberry_Pi_1.GND, Safety_Switch_Connector.1, LM1085.input_voltage, C1.-, C2.-, X1.GND, C3.0
  N1: Raspberry_Pi_1.GIPO17, R4.Pin_1, C3.1
  N2: Raspberry_Pi_1.GIPO27, R2.Pin_1
  N3: Raspberry_Pi_1.GIPO22, R3.Pin_1
  N4: Raspberry_Pi_1.GIPO24, Safety_Switch_Connector.3
  N5: Raspberry_Pi_1.GIPO23, Treadmill_Connector.7
  N6: Raspberry_Pi_1.GIPO18, R1.Pin_1
  N7: Treadmill_Connector.2, LM1085.output_voltage, C2.+
  N8: Treadmill_Connector.3, R4.Pin_0
  N9: Treadmill_Connector.4, R1.Pin_0
  N10: Treadmill_Connector.5, R2.Pin_0
  N11: Treadmill_Connector.6, R3.Pin_0
  N12: Safety_Switch_Connector.2, LM1085.GND, C1.+, X1.VBUS

notes:
  1 - Black, ground
  2 - Red, +9 VDC
  3 - Green, Speed sensor, 0-5 VDC
  4 - Blue, PWM signal to set speed
  5 - Orange, Incline up
  6 - Yellow, Incline down
  7 - Violet, Incline sensor
  8 - Striped black, step counter (MC2100SDI)
  Powering the Pi
  The LM1085 converts the 7-13 VDC from the motor controller to 5 V and can supply 3 A to run the Pi. This is applied via the USB power on the Pi because it has protection circuitry that the GPIO power pins do not.
  Black - Ground
  Red - 7-13 VDC
  Green - Speed sensor
  Blue - PWM motor speed driver
  Orange - Incline up
  Yellow - Incline down
  Violet - Incline changing
  Grey - Unused?
  Raspberry Pi Pins
  11 (GPIO 17) Speed sensor
  12 (GPIO 18) PWM output
  13 (GPIO 27) Incline up
  15 (GPIO 22) Incline down
  16 (GPIO 23) Incline sensor
  18 (GPIO 24) Safety switch
  Resistors are used on the output lines to limit current draw.
  Inputs are pulled up, so can be directly connected.
